# Fritzing sketch CalculatorSchematic (saved by Fritzing 0.8.7b)
breadboards: 1

parts:
  Part1 = Arduino Nano (Rev3.0)
  LCD1 = LCD screen
  R1 = Trimmer Potentiometer [maximum_resistance=10kΩ package=THT]
  S1 = Pushbutton [package="[THT]"]
  S2 = Pushbutton [package="[THT]"]
  S3 = Pushbutton [package="[THT]"]
  S4 = Pushbutton [package="[THT]"]
  S5 = Pushbutton [package="[THT]"]
  R2 = Resistor [tolerance=±5% resistance=1k package=THT]
  R3 = Resistor [tolerance=±5% resistance=1k package=THT]
  R4 = Resistor [tolerance=±5% resistance=1k package=THT]
  R5 = Resistor [tolerance=±5% resistance=1k package=THT]
  R6 = Resistor [tolerance=±5% resistance=1k package=THT]

nets:
  N1: Part1.D1/TX, LCD1.RS
  GND: Part1.GND, LCD1.VSS, LCD1.R/W, LCD1.LED-, R1.leg2, R2.Pin_0, R3.Pin_0, R4.Pin_0, R5.Pin_0, R6.Pin_0
  N2: Part1.D2, LCD1.E
  N3: Part1.D3, LCD1.V0
  N4: Part1.D4, LCD1.DB4
  N5: Part1.D5, LCD1.DB5
  N6: Part1.D6, LCD1.DB6
  N7: Part1.D7, LCD1.DB7
  N8: Part1.D8, S5.Pin_1, S5.Pin_2, R6.Pin_1
  N9: Part1.D9, S4.Pin_1, S4.Pin_2, R5.Pin_1
  N10: Part1.D10, S3.Pin_1, S3.Pin_2, R4.Pin_1
  N11: Part1.D11/MOSI, S2.Pin_1, S2.Pin_2, R3.Pin_1
  N12: Part1.D12/MISO, S1.Pin_1, S1.Pin_2, R2.Pin_1
  5V: Part1.5V, LCD1.VDD, LCD1.LED+, R1.leg1, S1.Pin_3, S1.Pin_4, S2.Pin_3, S2.Pin_4, S3.Pin_3, S3.Pin_4, S4.Pin_3, S4.Pin_4, S5.Pin_3, S5.Pin_4
  N13: Part1.A5, R1.wiper
